# Fritzing sketch ConjuntoAtuador (saved by Fritzing 0.8.7b)
circuit board: 8.46667cm x 5.64444cm

parts:
  V1 = DC Power [voltage=5]
  Arduino_Pro_Mini_3_3v = Arduino Pro Mini v13
  BT1 = Bluetooth HC-06d [package=THT]
  RC1 = nRF24L01 [package=module]
  M1 = DC Motor
  Q1 = npn-Powertransistor [package="TO220 [THT]"]
  M2 = DC Motor
  Q2 = npn-Powertransistor [package="TO220 [THT]"]
  M3 = DC Motor
  Q3 = npn-Powertransistor [package="TO220 [THT]"]
  M4 = DC Motor
  Q4 = npn-Powertransistor [package="TO220 [THT]"]
  M5 = DC Motor
  Q5 = npn-Powertransistor [package="TO220 [THT]"]
  PCM = IC, SIP package, 4 pins
  X1 = USB Connectors [package=usb-a-s-nosilk-female]  # not connected

nets:
  N1: V1.V-, PCM.pin4
  N2: Arduino_Pro_Mini_3_3v.D0/TX, BT1.RXD
  N3: Arduino_Pro_Mini_3_3v.D1/RX, BT1.TXD
  GND: Arduino_Pro_Mini_3_3v.GND, BT1.GND, RC1.GND, M1.pin_2, M2.pin_2, M3.pin_2, M4.pin_2, M5.pin_2, PCM.pin3
  N4: Arduino_Pro_Mini_3_3v.RAW, BT1.VCC, Q1.collector, Q2.collector, Q3.collector, Q4.collector, Q5.collector, PCM.pin2
  VCC: Arduino_Pro_Mini_3_3v.VCC, RC1.VCC
  N5: Arduino_Pro_Mini_3_3v.D13/SCK, RC1.SCK
  N6: Arduino_Pro_Mini_3_3v.D12/MISO, RC1.MISO
  N7: Arduino_Pro_Mini_3_3v.D11_PWM/MOSI, RC1.MOSI
  N8: Arduino_Pro_Mini_3_3v.D10_PWM/SS, RC1.CSN
  N9: Arduino_Pro_Mini_3_3v.D9_PWM, RC1.CE
  N10: Arduino_Pro_Mini_3_3v.D6_PWM, Q5.base
  N11: Arduino_Pro_Mini_3_3v.D5_PWM, Q4.base
  N12: Arduino_Pro_Mini_3_3v.D4, Q3.base
  N13: Arduino_Pro_Mini_3_3v.D3_PWM, Q2.base
  N14: Arduino_Pro_Mini_3_3v.D2, Q1.base
  N15: M1.pin_1, Q1.emitter
  N16: M2.pin_1, Q2.emitter
  N17: M3.pin_1, Q3.emitter
  N18: M4.pin_1, Q4.emitter
  N19: M5.pin_1, Q5.emitter

custom parts:
  Bluetooth HC-06d: Bluetooth HC-06 - face down, pins down 16.5mm x 37.5mm PCB
  nRF24L01: nRF24L01 module
