# Fritzing sketch ConjuntoDeControle (saved by Fritzing 0.8.7b)
circuit board: 8.46667cm x 5.64444cm

parts:
  V1 = DC Power [voltage=5]
  Arduino_Pro_Mini_3_3v = Arduino Pro Mini v13
  RC1 = nRF24L01 [package=module]
  PCM = IC, SIP package, 4 pins
  X1 = USB Connectors [package=usb-a-s-nosilk-female]  # not connected
  S1 = Pushbutton [package="[THT]"]

nets:
  N1: V1.V-, PCM.pin4
  GND: Arduino_Pro_Mini_3_3v.GND, RC1.GND, PCM.pin3
  N2: Arduino_Pro_Mini_3_3v.RAW, PCM.pin2
  VCC: Arduino_Pro_Mini_3_3v.VCC, RC1.VCC, S1.Pin_3, S1.Pin_4
  N3: Arduino_Pro_Mini_3_3v.D13/SCK, RC1.SCK
  N4: Arduino_Pro_Mini_3_3v.D12/MISO, RC1.MISO
  N5: Arduino_Pro_Mini_3_3v.D11_PWM/MOSI, RC1.MOSI
  N6: Arduino_Pro_Mini_3_3v.D10_PWM/SS, RC1.CSN
  N7: Arduino_Pro_Mini_3_3v.D9_PWM, RC1.CE
  N8: Arduino_Pro_Mini_3_3v.D2, S1.Pin_1, S1.Pin_2

custom parts:
  nRF24L01: nRF24L01 module
