# Fritzing sketch controlador (saved by Fritzing 0.8.7b)
circuit board: 6.19451cm x 5.07378cm

parts:
  J5 = Basic Servo
  J3 = Basic Servo
  J4 = Basic Servo
  J1 = Basic Servo
  S1 = Pushbutton [package="[SMD]"]
  R2 = Resistor [tolerance=±5% resistance=220 package=THT]
  S2 = Pushbutton [package="[SMD]"]
  PCM = TP4056 [chip_label=TP4056 package="DIP (Dual Inline) [THT]"]
  ESP32s = ESP32S-HiLetgo [part_number=ESP32S-HiLetgo]
  R1 = Resistor [tolerance=±5% resistance=220 package=THT]
  J2 = Basic Servo
  U1 = Mini-360 DC-DC Buck converter [package=THT]
  B = Battery block 9V

nets (from the schematic view):
  GND: J5.gnd, J3.gnd, J4.gnd, J1.gnd, PCM.pin6, ESP32s.GND, J2.gnd
  VCC: J5.vcc, J3.vcc, J4.vcc, J1.vcc, PCM.pin3, ESP32s.VIN, J2.vcc
  N1: J5.pulse, ESP32s.GPIO27
  N2: J3.pulse, ESP32s.GPIO25
  N3: J4.pulse, ESP32s.GPIO26
  N4: J1.pulse, ESP32s.GPIO32
  N5: S1.Pin_1, S1.Pin_2, ESP32s.GPIO4
  N6: S1.Pin_3, S1.Pin_4, R1.Pin_1
  N7: R2.Pin_0, ESP32s.3.3, R1.Pin_0
  N8: R2.Pin_1, S2.Pin_1, S2.Pin_2
  N9: S2.Pin_3, S2.Pin_4, ESP32s.GPIO16
  N10: PCM.pin4, U1.OUT+
  N11: PCM.pin5, U1.OUT-
  N12: ESP32s.GPIO33, J2.pulse
  N13: U1.IN-, B.-
  N14: U1.IN+, B.+

custom parts:
  TP4056: A DIP stand-in part for whatever IC you want. With 6 pins on a 300mil dual inline package (DIP) footprint.
  ESP32S-HiLetgo: HiLetgo ESP-WROOM-32 ESP32 ESP-32S Development Board 2.4GHz Dual-Mode WiFi + Bluetooth Dual Cores Microcontroller The ESP32 integrated with Antenna switches, RF Balun, power amplifiers, low-noise amplifiers, filters, and management modules, and the entire solution occupies the least area of PCB. 2.4 GHz Wi-Fi plus Bluetooth dual-mode chip, with TSMC Ultra-low power consumption 40nm technology,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
  Mini-360 DC-DC Buck converter: Mini-360 DC-DC Buck converter. Tiny buck step down voltage converter, input voltage 4.75 to 23V output 1 to 17V adjustable. Available from ebay and the like.
